# Fritzing sketch Knock_box (saved by Fritzing 0.9.9b)

parts:
  Part1 = Arduino Nano (Rev3.0)
  VCC_(6V) = 10 x AA Battery Mount
  Trasistor_(TIP_120) = TIP120 Hi-Current Darlington Transistor
  R1 = Resistor [tolerance=±5% resistance=220 package="2512 [SMD]"]
  D1 = Rectifier Diode [part_number=1N4001 package="Melf DO-213 AB [SMD]"]
  VCC_(6V)1 = 10 x AA Battery Mount
  Solenoid = Solenoid
  Piezoelectric_Sensor1 = Piezoelectric Sensor

nets:
  GND: Part1.GND, Trasistor_(TIP_120).EMITTER, VCC_(6V)1.+, Piezoelectric_Sensor1.GND
  N1: Part1.D2, R1.Pin_1
  N2: Part1.A7, Piezoelectric_Sensor1.VCC
  N3: VCC_(6V).-, D1.cathode, Solenoid.pin2
  N4: VCC_(6V).+, VCC_(6V)1.-
  N5: Trasistor_(TIP_120).BASE, R1.Pin_0
  N6: Trasistor_(TIP_120).COLLECTOR, D1.anode, Solenoid.pin1

custom parts:
  10 x AA Battery Mount: A 10 x AA battery pack (4.8 Volts with recharables)
  Piezoelectric Sensor: Piezoelectric sensor.
